# Fritzing sketch MotionLED (saved by Fritzing 0.9.3b)
breadboards: 1

parts:
  Q2 = Basic FET N-Channel [part_number=IRF540N package="DPak [SMD]"]
  J1 = Power Jack [package=power_jack_slot]
  M1 = RioRand LM2596
  J2 = Camdenboss CTB0158-2 [part_number=CTB0158-2 package=THT]
  PIR1 = PIR sensor
  Part1 = Logic Level Converter
  U1 = NodeMCU V1.0

nets:
  N1: Q2.Gate, Part1.TX2_HV
  N2: Q2.drain, J2.pin1
  N3: Q2.source, J1.GND, M1.Pin_1
  N4: J1.PWR, M1.Pin_2, J2.pin2
  VDD: M1.Pin_3, PIR1.VDD, Part1.HV, U1.Vin
  GND: M1.Pin_4, PIR1.GND, Part1.GND, U1.GND
  N5: PIR1.SIG, U1.D2
  N6: Part1.TX2_LV, U1.D1
  N7: Part1.LV, U1.3V3

notes:
  12V DC IN
  12V DC OUT
  5V DC OUT

custom parts:
  NodeMCU V1.0: ESP8266 based NodeMCU
